# Fritzing sketch Devre_Semasi (saved by Fritzing 0.9.3b)
breadboards: 1

parts:
  U1 = GAS_SENSOR [package=mq-3]
  DHT1 = DHT11 Humitidy and Temperature Sensor
  Parça1 = IFR520 MOS module [package=THT]
  Parça2 = Arduino Mega 2560 (Rev3)
  M1 = DC Motor

nets:
  N1: U1.B1, Parça2.A0
  VDD: U1.H1, DHT1.VDD, Parça1.VCC, Parça1.VIN, Parça2.5V
  GND: U1.H2, DHT1.GND, Parça1.GND, Parça2.GND
  N2: DHT1.DATA, Parça2.D2_PWM
  N3: Parça1.SIG, Parça2.D3_PWM
  N4: Parça1.V+, M1.pin_1
  N5: Parça1.V-, M1.pin_2

notes:
  Analog Çıkış
  DC Fan Motor

custom parts:
  DHT11 Humitidy and Temperature Sensor: DHT11 Humidity and Temperature Sensor
